// Logisim project tarea1.circ as structural Verilog: 5 circuits, main circuit main
module deco (
  input  x1,
  input  x0,
  output y0,
  output y1,
  output y2,
  output y3,
  output y4,
  output y5,
  output y6
);

  wire not_1_out;

  not not_1 (not_1_out, x0);
  or or_1 (y1, x1, x0);
  and and_1 (y4, x1, not_1_out);

  assign y0 = x1;
  assign y2 = x0;
  assign y3 = x1;
  assign y5 = 1'b0;
  assign y6 = x1;
endmodule

module main (
  input  in_1,
  input  in_2
);

  wire deco_1_y0, deco_1_y1, deco_1_y2, deco_1_y3, deco_1_y4, deco_1_y5, deco_1_y6;

  deco deco_1 (
    .y0(deco_1_y0), .y1(deco_1_y1), .y2(deco_1_y2), .y3(deco_1_y3), .y4(deco_1_y4), .y5(deco_1_y5),
    .y6(deco_1_y6), .x0(in_1), .x1(in_2));
  _7_Segment_Display u_7_segment_display_1 (
    .g(deco_1_y6), .f(deco_1_y5), .a(deco_1_y0), .b(deco_1_y1), .e(deco_1_y4), .d(deco_1_y3), .c(deco_1_y2));  // open: dp
endmodule

module DecoBlock (
  input  [1:0] I0,
  input  [1:0] I1,
  input  [1:0] I2,
  input  [1:0] I3,
  output [6:0] O0,
  output [6:0] O1,
  output [6:0] O2,
  output [6:0] O3
);

  deco deco_1 (
    .y0(O0[0]), .y1(O0[1]), .y2(O0[2]), .y3(O0[3]), .y4(O0[4]), .y5(O0[5]), .y6(O0[6]), .x0(I0[0]), .x1(I0[1]));
  deco deco_2 (
    .y0(O1[0]), .y1(O1[1]), .y2(O1[2]), .y3(O1[3]), .y4(O1[4]), .y5(O1[5]), .y6(O1[6]), .x0(I1[0]), .x1(I1[1]));
  deco deco_3 (
    .y0(O2[0]), .y1(O2[1]), .y2(O2[2]), .y3(O2[3]), .y4(O2[4]), .y5(O2[5]), .y6(O2[6]), .x0(I2[0]), .x1(I2[1]));
  deco deco_4 (
    .y0(O3[0]), .y1(O3[1]), .y2(O3[2]), .y3(O3[3]), .y4(O3[4]), .y5(O3[5]), .y6(O3[6]), .x0(I3[0]), .x1(I3[1]));
endmodule

module vicinity (
  input  [1:0] P1,
  input  [1:0] P2,
  output out_3
);

  wire and_1_out, and_2_out, and_3_out, and_4_out, and_5_out, and_6_out, and_7_out, and_8_out, not_1_out,
       not_2_out, not_3_out, not_4_out;

  not not_1 (not_1_out, P1[1]);
  not not_2 (not_2_out, P1[0]);
  not not_3 (not_3_out, P2[1]);
  not not_4 (not_4_out, P2[0]);
  and and_1 (and_1_out, not_1_out, not_2_out, not_3_out, P2[0]);
  and and_2 (and_2_out, not_1_out, not_2_out, P2[1], not_4_out);
  and and_3 (and_3_out, not_1_out, P1[0], not_3_out, not_4_out);
  and and_4 (and_4_out, not_1_out, P1[0], P2[1], P2[0]);
  and and_5 (and_5_out, P1[1], P1[0], not_3_out, P2[0]);
  or or_1 (out_3, and_1_out, and_2_out, and_3_out, and_4_out, and_5_out, and_6_out, and_7_out, and_8_out);
  and and_6 (and_6_out, P1[1], P1[0], P2[1], not_4_out);
  and and_7 (and_7_out, P1[1], not_2_out, not_3_out, not_4_out);
  and and_8 (and_8_out, P1[1], not_2_out, P2[1], P2[0]);
endmodule

module control_cursor (
  output [3:0] x,
  output out_2,
  output out_3,
  output out_4,
  output [3:0] y,
  output out_6
);

  Joystick joystick_1 (.x(x), .y(y));
  Comparator #(.width(4), .mode("unsigned")) comparator_1 (.a(x), .b(4'b0100), .lt(out_3));  // open: gt, eq
  Comparator #(.width(4), .mode("unsigned")) comparator_2 (.a(x), .b(4'b1100), .gt(out_4));  // open: eq, lt
  Comparator #(.width(4), .mode("unsigned")) comparator_3 (.a(y), .b(4'b0100), .lt(out_2));  // open: gt, eq
  Comparator #(.width(4), .mode("unsigned")) comparator_4 (.a(y), .b(4'b1100), .gt(out_6));  // open: eq, lt
endmodule
